# Fritzing sketch disc (saved by Fritzing 0.7.12b)
breadboards: 1

parts:
  Nano1 = Arduino Nano v3.0
  Part1 = Triple Axis Accelerometer Breakout - ADXL345
  IC1 = IC, DIP package, 24 pins [chip_label=Wixel]
  J1 = Generic female header - 8 pins [part_number=TCS230 package=THT]
  J2 = Generic female header - 4 pins [part_number="Strip 1" package=THT]
  R1 = 10k Ω Resistor [package=THT]
  R2 = 10k Ω Resistor [package=THT]
  R3 = 10k Ω Resistor [package=THT]

nets:
  N1: Nano1.D0RX, IC1.pin8, R2.Pin_0, R3.Pin_0
  GND: Nano1.GND, Part1.GND, IC1.pin1, J1.pin6, J2.pin1, R1.Pin_0
  N2: Nano1.D2, J1.pin4
  N3: Nano1.D3, J1.pin3
  N4: Nano1.D4, J1.pin7
  N5: Nano1.D5, J1.pin8
  N6: Nano1.D6, J1.pin2
  N7: Nano1.D7, J1.pin1
  N8: Nano1.D12, J2.pin2
  N9: Nano1.D13, J2.pin3
  N10: Nano1.A4, Part1.SDA
  N11: Nano1.A5, Part1.SCL
  +5V: Nano1.+5V, Part1.VCC, IC1.pin2, J1.pin5, J2.pin4
  N12: IC1.pin9, R3.Pin_1
  N13: R1.Pin_1, R2.Pin_1
