# Fritzing sketch jacket (saved by Fritzing 0.7.12b)
breadboards: 2

parts:
  U1 = Arduino Mega
  IC1 = IC, DIP package, 14 pins [chip_label=74LS125]
  IC2 = IC, DIP package, 14 pins [chip_label=74LS125]
  IC3 = IC, DIP package, 8 pins [chip_label=MSGEQ7]
  IC4 = IC, DIP package, 8 pins [chip_label=TS922]
  U2 = Voltage Regulator - 3.3V [package="TO220 [THT]"]
  Q1 = Basic FET N-Channel [part_number=2N7000 package="TO220 [THT]"]
  Q2 = Basic FET N-Channel [part_number=2N7000 package="TO220 [THT]"]
  Part1 = Bluetooth Mate Silver
  IC5 = IC, DIP package, 24 pins [chip_label=Wixel]
  J2 = Generic female header - 3 pins [part_number="Helmet Microphone (Adafruit 1063)" package=THT]
  J3 = Generic female header - 3 pins [part_number="Helmet Screen (Adafruit 784)" package=THT]
  J4 = Generic female header - 4 pins [part_number="Strip 2" package=THT]
  J5 = Generic female header - 4 pins [part_number="Strip 1" package=THT]
  J6 = Generic female header - 4 pins [part_number="Strip 3" package=THT]
  J7 = Generic female header - 4 pins [part_number="Strip 4" package=THT]
  R1 = 10k Ω Resistor [package=THT]
  R2 = 10k Ω Resistor [package=THT]
  R3 = 10k Ω Resistor [package=THT]
  R4 = 10k Ω Resistor [package=THT]
  C1 = Ceramic Capacitor [package=THT]
  C2 = Ceramic Capacitor [package=THT]
  J8 = Generic female header - 4 pins [part_number=Nunchuk package=THT]
  C3 = Electrolytic Capacitor [package=THT]
  R5 = 10k Ω Resistor [package=THT]
  R6 = 10k Ω Resistor [package=THT]
  R7 = 10k Ω Resistor [package=THT]
  R8 = 10k Ω Resistor [package=THT]
  R9 = 10k Ω Resistor [package=THT]
  R10 = 10k Ω Resistor [package=THT]
  R11 = 10k Ω Resistor [package=THT]
  R12 = 100k Ω Resistor [package=THT]
  R13 = 100k Ω Resistor [package=THT]
  C4 = Ceramic Disk Capacitor [part_number=33pf package=THT]
  C6 = Ceramic Capacitor [package=THT]
  C8 = Ceramic Capacitor [package=THT]
  C9 = Ceramic Capacitor [package=THT]
  D1 = Rectifier Diode [part_number="Germanium Diode" package=THT]
  D2 = Rectifier Diode [part_number="Germanium Diode" package=THT]
  R14 = Trimmer Potentiometer [maximum_resistance=100kΩ part_number=50k package=THT]
  R15 = 10k Ω Resistor [package=THT]
  R16 = 100k Ω Resistor [package=THT]
  R17 = 100k Ω Resistor [package=THT]
  C10 = Electrolytic Capacitor [package=THT]

nets:
  GND: U1.GND, IC1.pin7, IC2.pin7, IC3.pin2, IC4.pin4, U2.GND, Part1.GND, IC5.pin1, J2.pin3, J3.pin1, J4.pin1, J5.pin1, J6.pin1, J7.pin1, R1.Pin_0, R2.Pin_0, R3.Pin_0, R4.Pin_0, C1.pin_1, C2.pin_1, J8.pin4, C3.-, R11.Pin_1, C4.pin_1, C8.pin_0, C9.pin_0, R17.Pin_1, C10.-
  N1: U1.D0RX, IC3.pin3
  N2: U1.3V3, IC4.pin8, J2.pin1, R16.Pin_1, C10.+
  N3: U1.+5V#18, IC1.pin14, IC2.pin14, U2.input_voltage, J4.pin4, J5.pin4, J6.pin4, J7.pin4, C1.pin_0, C2.pin_0, R5.Pin_1, R8.Pin_1
  N4: U1.A2, IC3.pin4
  N5: U1.A3, IC3.pin6
  N6: U1.D14, J3.pin2
  N7: U1.D16, Part1.RX_5V
  N8: U1.D17, Part1.TX_5V
  N9: U1.D18, R9.Pin_1, R10.Pin_0
  N10: U1.D19, IC5.pin17
  N11: U1.D20, Q1.drain, R5.Pin_0
  N12: U1.D21, Q2.drain, R8.Pin_0
  N13: U1.D48, IC2.pin1, IC2.pin13
  N14: U1.D49, IC2.pin4, IC2.pin10
  N15: U1.D50, IC1.pin1, IC1.pin13
  N16: U1.D51, IC1.pin4, IC1.pin10
  N17: U1.D52, IC1.pin2, IC1.pin5, IC2.pin2, IC2.pin5
  N18: U1.D53, IC1.pin9, IC1.pin12, IC2.pin9, IC2.pin12
  N19: U1.+5V#80, IC3.pin1, Part1.VCC, IC5.pin2, R12.Pin_1, C9.pin_1
  N20: U1.+5V#81, J3.pin3
  N21: IC1.pin3, J6.pin3
  N22: IC1.pin6, J7.pin3
  N23: IC1.pin8, J7.pin2, R2.Pin_1
  N24: IC1.pin11, J6.pin2, R4.Pin_1
  N25: IC2.pin3, J5.pin3
  N26: IC2.pin6, J4.pin3
  N27: IC2.pin8, J4.pin2, R3.Pin_1
  N28: IC2.pin11, J5.pin2, R1.Pin_1
  N29: IC3.pin5, C6.pin_0
  N30: IC3.pin7, C8.pin_1
  N31: IC3.pin8, R13.Pin_0, C4.pin_0
  N32: IC4.pin1, C6.pin_1, D1.cathode, D2.anode
  N33: IC4.pin2, D1.anode, D2.cathode, R15.Pin_0
  N34: IC4.pin3, R16.Pin_0, R17.Pin_0
  N35: IC4.pin5, J2.pin2
  N36: IC4.pin6, IC4.pin7, R14.wiper
  N37: U2.output_voltage, Q1.gate, Q2.gate, J8.pin1, C3.+, R6.Pin_0, R7.Pin_0
  N38: Q1.source, J8.pin2, R6.Pin_1
  N39: Q2.source, J8.pin3, R7.Pin_1
  N40: IC5.pin16, R9.Pin_0
  N41: R10.Pin_1, R11.Pin_0
  N42: R12.Pin_0, R13.Pin_1
  N43: R14.leg1, R15.Pin_1
